# Fritzing sketch ndc_arduinouno_esp8266 (saved by Fritzing 0.9.3b)
circuit board: 11.3648cm x 5.72585cm

parts:
  Arduino_Uno = Arduino Uno (Rev3) - ICSP
  Wi-Fi_ESP8266 = ESP8266 WiFi Module [part_number=ESP8266]

nets:
  GND: Arduino_Uno.GND, Wi-Fi_ESP8266.GND
  N1: Arduino_Uno.D3_PWM, Wi-Fi_ESP8266.TXD
  N2: Arduino_Uno.D4, Wi-Fi_ESP8266.RXD
  3V3: Arduino_Uno.3V3, Wi-Fi_ESP8266.VCC

notes:
  Pinouts: ESP8266 TX to Arduino Uno Digital Pin 3
  ESP8266 RX to Arduino Uno Digital Pin 4

// code stored in the sketch: ESP8266.ino
//www.amiedd.com
//Arduino Uno, Unity connection with ESP8266

#include <SoftwareSerial.h>

#define ESP8266_TX    3
#define ESP8266_RX    4
#define ESP8266_BAUD    9600

SoftwareSerial esp8266(ESP8266_TX, ESP8266_RX); // SoftwareSerial(RX, TX)

void setup()
{
  Serial.begin(ESP8266_BAUD);
  esp8266.begin(ESP8266_BAUD);
}

void loop()
{
  while(Serial.available() > 0)
    esp8266.write(Serial.read());

  while(esp8266.available() > 0)
    Serial.write(esp8266.read());
}
