# Fritzing sketch NDC_ArduinoUno_Buzzer (saved by Fritzing 0.9.3b)
circuit board: 8.78074cm x 5.85644cm

parts:
  Arduino_Uno = Arduino Uno (Rev3)
  Buzzer = Buzzer 12mm [package=buzzer-ccv-kit]
  Resistor = Resistor [tolerance=±5% resistance=220 package="2512 [SMD]"]

nets:
  N1: Arduino_Uno.GND, Resistor.Pin_1
  N2: Arduino_Uno.D2, Buzzer.2
  N3: Buzzer.1, Resistor.Pin_0
