# Fritzing sketch NDC_ArduinoUno_Servo (saved by Fritzing 0.9.3b)

parts:
  Arduino_Uno = Arduino Uno (Rev3)
  Servo = Basic Servo

nets:
  GND: Arduino_Uno.GND, Servo.gnd
  N1: Arduino_Uno.D2, Servo.pulse
  5V: Arduino_Uno.5V, Servo.vcc
