# Fritzing sketch Sensor (saved by Fritzing 0.9.3b)

parts:
  Part1 = Arduino Uno (Rev3)
  hc-sr1 = hc-sr04

nets:
  N1: Part1.D2, hc-sr1.Trig
  N2: Part1.D3_PWM, hc-sr1.VCC
  N3: Part1.5V, hc-sr1.Echo
  GND: Part1.GND, hc-sr1.GND
